// Logisim project 4lr_preob.circ as structural Verilog: 1 circuit, main circuit main
module main (
  input  x1,
  input  x2,
  input  x3,
  input  x4,
  output y1,
  output y2,
  output y3,
  output y4
);

  wire and_2_out, and_3_out, and_4_out, and_6_out, and_7_out, and_out, not_1_out, not_2_out, not_3_out,
       not_4_out;

  not not_1 (not_1_out, x1);
  not not_2 (not_2_out, x2);
  not not_3 (not_3_out, x3);
  not not_4 (not_4_out, x4);
  and \and  (and_out, x1, not_2_out, not_3_out);
  and and_2 (and_2_out, not_1_out, x2);
  and and_3 (and_3_out, not_1_out, not_2_out);
  and and_4 (and_4_out, not_2_out, not_3_out);
  and and_5 (y3, not_1_out, x3);
  and and_6 (and_6_out, x4, not_2_out, not_3_out);
  and and_7 (and_7_out, not_1_out, x4);
  or l (y1, and_out, and_2_out);
  or l_2 (y2, and_3_out, and_4_out);
  or l_3 (y4, and_6_out, and_7_out);

  // Notes on the sheet:
  //   !x1
  //   !x2
  //   !x3
  //   !x4
  //   x1
  //   x2
  //   !x2
  //   !x1
  //   x3
  //   x4
  //   !x4
  //   !x3
  //   x1
  //   !x2
  //   !x3
  //   !x1
  //   x2
  //   !x1
  //   !x2
  //   !x2
  //   !x3
  //   !x1
  //   x3
  //   x4
  //   !x2
  //   !x3
  //   !x1
  //   x4
endmodule
