// Logisim project 4lr_summator.circ as structural Verilog: 1 circuit, main circuit main
module main (
  input  x1,
  input  x2,
  input  x3,
  output S,
  output P
);

  wire and_2_out, and_3_out, and_4_out, and_5_out, and_6_out, and_out, not_1_out, not_2_out, not_3_out;

  not not_1 (not_1_out, x1);
  not not_2 (not_2_out, x2);
  not not_3 (not_3_out, x3);
  and \and  (and_out, x3, not_1_out, not_2_out);
  and and_2 (and_2_out, not_1_out, x2, not_3_out);
  and and_3 (and_3_out, x1, not_2_out, not_3_out);
  and and_4 (and_4_out, x1, x3);
  and and_5 (and_5_out, x1, x2);
  and and_6 (and_6_out, x2, x3);
  or l (S, and_out, and_2_out, and_3_out);
  or l_2 (P, and_4_out, and_5_out, and_6_out);

  // Notes on the sheet:
  //   !x1
  //   !x2
  //   !x3
  //   x1
  //   x2
  //   !x2
  //   !x3
  //   !x1
  //   x3
  //   x1
  //   x3
  //   x1
  //   x2
  //   x2
  //   x3
endmodule
