// Logisim project 5lr.circ as structural Verilog: 1 circuit, main circuit main
module main (
  input  V,
  output q1,
  output q2,
  output q3,
  output q4
);

  wire and_1_out, and_2_out, and_3_out, clock_1_out;

  and and_1 (and_1_out, V, q4, q3, q2);
  and and_2 (and_2_out, V, q4, q3);
  and and_3 (and_3_out, V, q4);
  Clock clock_1 (.out(clock_1_out));
  T_Flip_Flop t_ff_1 (.clk(clock_1_out), .T(and_1_out), .Q(q1));  // open: Qn, preset, reset, en
  T_Flip_Flop t_ff_2 (.clk(clock_1_out), .T(and_2_out), .Q(q2));  // open: Qn, preset, reset, en
  T_Flip_Flop t_ff_3 (.clk(clock_1_out), .T(and_3_out), .Q(q3));  // open: Qn, preset, reset, en
  T_Flip_Flop t_ff_4 (.clk(clock_1_out), .T(V), .Q(q4));  // open: Qn, preset, reset, en

  // Notes on the sheet:
  //   h1
  //   h2
  //   h3
  //   h4
  //   q2*
  //   q3*
  //   q4*
endmodule
